# Fritzing sketch ESP8266 Thermostat (saved by Fritzing 0.9.5d)
breadboards: 1

parts:
  U1 = ESP8266 NodeMCU LoLin module
  R1 = Temperature Sensor (Thermistor) [thermistor_type=NTC package=THT]
  R2 = Resistor [tolerance=±5% resistance=10k package=THT]

nets:
  N1: U1.D0, U1.RST
  N2: U1.3V3, R2.Pin_1
  N3: U1.GND, R1.pin_1
  N4: U1.A0, R1.pin_0, R2.Pin_0

custom parts:
  ESP8266 NodeMCU LoLin module: ESP8266 based NodeMCU
