# Fritzing sketch thermistor_schematic (saved by Fritzing 0.9.5d)

parts:
  R1 = Temperature Sensor (Thermistor) [thermistor_type=NTC package=THT]
  R2 = Resistor [tolerance=±5% resistance=10k package=THT]

nets:
  GND: R1.pin_0
  ADC: R1.pin_1, R2.Pin_1
  3.3V: R2.Pin_0
